# Fritzing sketch dark_activated_led (saved by Fritzing 0.9.4)
breadboards: 1

parts:
  Parça1 = Arduino Uno (Rev3)
  LED1 = LED - 5mm [color="Orange (620nm)" package="5 mm [THT]"]
  R1 = Photocell (LDR) [package=THT]
  R2 = Resistor [tolerance=±5% resistance=330 package=THT]
  R3 = Resistor [tolerance=±5% resistance=10k package=THT]

nets:
  N1: Parça1.A0, R1.pin_1, R3.Pin_0
  N2: Parça1.D3_PWM, R2.Pin_0
  N3: Parça1.5V, R1.pin_0
  N4: Parça1.GND, LED1.cathode, R3.Pin_1
  N5: LED1.anode, R2.Pin_1
